# Fritzing sketch Diagramas de conexion maquina chaskas (saved by Fritzing 0.9.3b)
circuit board: 8.46667cm x 5.64444cm
breadboards: 2

parts:
  DRV_1 = DRV 8825 Stepper Motor Carrier, High Current [part_number="DRV 8825"]
  DRV_2 = DRV 8825 Stepper Motor Carrier, High Current [part_number="DRV 8825"]
  DRV_3 = DRV 8825 Stepper Motor Carrier, High Current [part_number="DRV 8825"]
  DRV_4 = DRV 8825 Stepper Motor Carrier, High Current [part_number="DRV 8825"]
  DRV_5 = DRV 8825 Stepper Motor Carrier, High Current [part_number="DRV 8825"]
  DRV_6 = DRV 8825 Stepper Motor Carrier, High Current [part_number="DRV 8825"]
  HC-SR04_Sensor_1 = HC-SR04 Ultrasonic Distance Sensor
  HC-SR04_Sensor_2 = HC-SR04 Ultrasonic Distance Sensor
  HC-SR04_Sensor_4 = HC-SR04 Ultrasonic Distance Sensor
  HC-SR04_Sensor_3 = HC-SR04 Ultrasonic Distance Sensor
  HC-SR04_Sensor_5 = HC-SR04 Ultrasonic Distance Sensor
  HC-SR04_Sensor_6 = HC-SR04 Ultrasonic Distance Sensor
  DRV_7 = DRV 8825 Stepper Motor Carrier, High Current [part_number="DRV 8825"]
  DHT2 = DHT11 Humitidy and Temperature Sensor
  M1 = Stepper Motor - Bipolar
  M2 = Stepper Motor - Bipolar
  V1 = DC Power [voltage=12V]
  V2 = DC Power [voltage=5V]
  DHT1 = DHT11 Humitidy and Temperature Sensor
  DHT3 = DHT11 Humitidy and Temperature Sensor
  M3 = Stepper Motor - Bipolar
  M4 = Stepper Motor - Bipolar
  M5 = Stepper Motor - Bipolar
  M6 = Stepper Motor - Bipolar
  M7 = Stepper Motor - Bipolar
  U4 = MOC3010 [package=dil06]
  R1 = Resistor [tolerance=±5% resistance=180 package="0603 [SMD]"]
  BTA08600C = TRIAC [package=to-92]
  CA = AC Power [voltage=120V frequency=60]
  Motor_Chocomilera = DC Motor
  S1 = Round Pushbutton
  S2 = Round Pushbutton
  Componente1 = Arduino Mega ADK (Rev3)

nets:
  N1: DRV_1.ENABLE, Componente1.D48
  N2: DRV_1.RESET, DRV_1.SLEEP
  N3: DRV_1.STEP, Componente1.D37
  N4: DRV_1.DIRECTION, Componente1.D36
  N5: DRV_1.VOLTAGE_ST/_MT, DRV_2.VOLTAGE_ST/_MT, DRV_3.VOLTAGE_ST/_MT, DRV_4.VOLTAGE_ST/_MT, DRV_5.VOLTAGE_ST/_MT, DRV_6.VOLTAGE_ST/_MT, DRV_7.VOLTAGE_ST/_MT, S2.leg0
  GND: DRV_1.GROUND_ST/_MT, DRV_1.GROUND_LOG, DRV_2.GROUND_ST/_MT, DRV_2.GROUND_LOG, DRV_3.GROUND_ST/_MT, DRV_3.GROUND_LOG, DRV_4.GROUND_ST/_MT, DRV_4.GROUND_LOG, DRV_5.GROUND_ST/_MT, DRV_5.GROUND_LOG, DRV_6.GROUND_ST/_MT, DRV_6.GROUND_LOG, HC-SR04_Sensor_1.ECHO, HC-SR04_Sensor_2.ECHO, HC-SR04_Sensor_4.ECHO, HC-SR04_Sensor_3.ECHO, HC-SR04_Sensor_5.ECHO, HC-SR04_Sensor_6.ECHO, DRV_7.GROUND_ST/_MT, DRV_7.GROUND_LOG, DHT2.GND, DHT1.GND, DHT3.GND, U4.2
  N6: DRV_1.OUT_2B, M7.A
  N7: DRV_1.OUT_2A, M7.C
  N8: DRV_1.OUT_1A, M7.B
  N9: DRV_1.OUT_1B, M7.D
  VCC: DRV_1.VOLTAGE_DD, DRV_2.VOLTAGE_DD, DRV_3.VOLTAGE_DD, DRV_4.VOLTAGE_DD, DRV_5.VOLTAGE_DD, DRV_6.VOLTAGE_DD, HC-SR04_Sensor_1.VCC, HC-SR04_Sensor_2.VCC, HC-SR04_Sensor_4.VCC, HC-SR04_Sensor_3.VCC, HC-SR04_Sensor_5.VCC, HC-SR04_Sensor_6.VCC, DRV_7.VOLTAGE_DD, DHT2.VDD, DHT1.VDD, DHT3.VDD, S1.leg0
  N10: DRV_2.ENABLE, Componente1.D49
  N11: DRV_2.RESET, DRV_2.SLEEP
  N12: DRV_2.STEP, Componente1.D39
  N13: DRV_2.DIRECTION, Componente1.D38
  N14: DRV_2.OUT_2B, M2.A
  N15: DRV_2.OUT_2A, M2.C
  N16: DRV_2.OUT_1A, M2.B
  N17: DRV_2.OUT_1B, M2.D
  N18: DRV_3.ENABLE, Componente1.D50/MISO
  N19: DRV_3.RESET, DRV_3.SLEEP
  N20: DRV_3.STEP, Componente1.D41
  N21: DRV_3.DIRECTION, Componente1.D40
  N22: DRV_3.OUT_2B, M3.A
  N23: DRV_3.OUT_2A, M3.C
  N24: DRV_3.OUT_1A, M3.B
  N25: DRV_3.OUT_1B, M3.D
  N26: DRV_4.ENABLE, Componente1.D51/MOSI
  N27: DRV_4.RESET, DRV_4.SLEEP
  N28: DRV_4.STEP, Componente1.D43
  N29: DRV_4.DIRECTION, Componente1.D42
  N30: DRV_4.OUT_2B, M4.A
  N31: DRV_4.OUT_2A, M4.C
  N32: DRV_4.OUT_1A, M4.B
  N33: DRV_4.OUT_1B, M4.D
  N34: DRV_5.ENABLE, Componente1.D52/SCK
  N35: DRV_5.RESET, DRV_5.SLEEP
  N36: DRV_5.STEP, Componente1.D45
  N37: DRV_5.DIRECTION, Componente1.D44
  N38: DRV_5.OUT_2B, M5.A
  N39: DRV_5.OUT_2A, M5.C
  N40: DRV_5.OUT_1A, M5.B
  N41: DRV_5.OUT_1B, M5.D
  N42: DRV_6.ENABLE, Componente1.D53/SS
  N43: DRV_6.RESET, DRV_6.SLEEP
  N44: DRV_6.STEP, Componente1.D47
  N45: DRV_6.DIRECTION, Componente1.D46
  N46: DRV_6.OUT_2B, M6.A
  N47: DRV_6.OUT_2A, M6.C
  N48: DRV_6.OUT_1A, M6.B
  N49: DRV_6.OUT_1B, M6.D
  N50: HC-SR04_Sensor_1.TRIG, Componente1.D22
  N51: HC-SR04_Sensor_1.GND, Componente1.D23
  N52: HC-SR04_Sensor_2.TRIG, Componente1.D24
  N53: HC-SR04_Sensor_2.GND, Componente1.D25
  N54: HC-SR04_Sensor_4.TRIG, Componente1.D28
  N55: HC-SR04_Sensor_4.GND, Componente1.D29
  N56: HC-SR04_Sensor_3.TRIG, Componente1.D26
  N57: HC-SR04_Sensor_3.GND, Componente1.D27
  N58: HC-SR04_Sensor_5.TRIG, Componente1.D30
  N59: HC-SR04_Sensor_5.GND, Componente1.D31
  N60: HC-SR04_Sensor_6.TRIG, Componente1.D32
  N61: HC-SR04_Sensor_6.GND, Componente1.D33
  N62: DRV_7.ENABLE, Componente1.D6_PWM
  N63: DRV_7.RESET, DRV_7.SLEEP
  N64: DRV_7.STEP, Componente1.D8_PWM
  N65: DRV_7.DIRECTION, Componente1.D7_PWM
  N66: DRV_7.OUT_2B, M1.A
  N67: DRV_7.OUT_2A, M1.C
  N68: DRV_7.OUT_1A, M1.B
  N69: DRV_7.OUT_1B, M1.D
  N70: DHT2.DATA, Componente1.D35
  N71: V1.V+, S2.leg1
  GND_2: V1.V-, V2.V-
  N72: V2.V+, S1.leg1
  N73: DHT1.DATA, Componente1.D34
  N74: DHT3.DATA, Componente1.D2_PWM
  N75: U4.1, Componente1.D5_PWM
  N76: U4.4, BTA08600C.G
  N77: U4.6, R1.Pin_0
  N78: R1.Pin_1, BTA08600C.M2, Motor_Chocomilera.pin_2
  N79: BTA08600C.M1, CA.V+
  N80: CA.V-, Motor_Chocomilera.pin_1

notes:
  Elaboración de Chaskas, Diagrama eléctrico de una máquina cuyo objetivo es automatizar el proceso de elaboración de una Chaska, 3

custom parts:
  DHT11 Humitidy and Temperature Sensor: DHT11 Humidity and Temperature Sensor
  MOC3010: Opto-isolated TRIAC
  Round Pushbutton: A generic pushbutton.
